# Fritzing sketch Untitled Sketch (saved by Fritzing 0.9.3b)
circuit board: 8.46667cm x 5.64444cm
breadboards: 2

parts:
  LCD1 = LCD screen
  Part2 = Arduino Cellular Shield
  Part3 = Arduino Mega 2560 (Rev3)
  S1 = Pushbutton [package="[THT]"]
  S2 = Pushbutton [package="[THT]"]
  S3 = Pushbutton [package="[THT]"]
  S4 = Pushbutton [package="[THT]"]
  S5 = Pushbutton [package="[THT]"]
  S6 = Pushbutton [package="[THT]"]
  R1 = Resistor [tolerance=±5% resistance=4.7k package=THT]
  R2 = Resistor [tolerance=±5% resistance=4.7k package=THT]
  R3 = Resistor [tolerance=±5% resistance=4.7k package=THT]
  R4 = Resistor [tolerance=±5% resistance=4.7k package=THT]
  R5 = Resistor [tolerance=±5% resistance=4.7k package=THT]
  R6 = Resistor [tolerance=±5% resistance=4.7k package=THT]
  U1 = ENCODER-QUADRATURE [package=encoder-16mm-quad]
  LED2 = LED - 5mm [color="Red (633nm)" package="5 mm [THT]"]
  LED1 = smd LED [color="Green (555nm)" package="0805 [SMD]"]
  R7 = Resistor [tolerance=±5% resistance=330 package=THT]
  R8 = Resistor [tolerance=±5% resistance=330 package=THT]
  R9 = Resistor [tolerance=±5% resistance=330 package=THT]
  R10 = Resistor [tolerance=±5% resistance=330 package=THT]

nets:
  VSS: LCD1.VSS, LCD1.R/W, LCD1.LED-, Part3.GND, R1.Pin_1, R2.Pin_1, R4.Pin_1, R5.Pin_1, R6.Pin_1, U1.C, R7.Pin_1, R8.Pin_1, R9.Pin_1, R10.Pin_1
  N1: LCD1.VDD, R10.Pin_0
  N2: LCD1.V0, U1.B
  N3: LCD1.RS, Part3.D12_PWM
  N4: LCD1.E, Part3.D11_PWM
  N5: LCD1.DB4, Part3.D10_PWM
  N6: LCD1.DB5, Part3.D6_PWM
  N7: LCD1.DB6, Part3.D5_PWM
  N8: LCD1.DB7, Part3.D4_PWM
  N9: LCD1.LED+, R9.Pin_0
  N10: Part2.RX-I, Part3.D0_RX0
  N11: Part2.TX-O, Part3.D1_TX0
  N12: Part3.5V, S1.Pin_1, S1.Pin_2, S2.Pin_1, S3.Pin_1, S3.Pin_2, S4.Pin_1, S5.Pin_1, S5.Pin_2, S6.Pin_1, S6.Pin_2, U1.A
  N13: Part3.D2_PWM, LED2.anode
  N14: Part3.D3_PWM, LED1.anode
  N15: S1.Pin_3, S1.Pin_4, R1.Pin_0
  N16: S2.Pin_3, S2.Pin_4, R2.Pin_0
  N17: S3.Pin_3, S3.Pin_4, R3.Pin_0
  N18: S4.Pin_3, R4.Pin_0
  N19: S5.Pin_3, R5.Pin_0
  N20: S6.Pin_3, S6.Pin_4, R6.Pin_0
  N21: LED2.cathode, R8.Pin_0
  N22: LED1.cathode, R7.Pin_0

// code stored in the sketch: Untitled.ino

